# Fritzing sketch Altimeter (saved by Fritzing 0.9.6b)

parts:
  Mod1 = Raspberry Pi Pico
  Driver1 = 28BYJ-48 Driver Module [part_number=ULN2003 package=THT]
  Driver2 = 28BYJ-48 Driver Module [part_number=ULN2003 package=THT]
  SM1 = 28BYJ-48 Stepper Motor [part_number=28BYJ-48]
  SM2 = 28BYJ-48 Stepper Motor [part_number=28BYJ-48]
  RE1 = KY-040 Rotary encoder [package=THT]  # not connected

nets:
  N1: Mod1.pin_14, Driver2.IN1
  N2: Mod1.pin_15, Driver2.IN2
  N3: Mod1.pin_16, Driver2.IN3
  N4: Mod1.pin_17, Driver2.IN4
  N5: Mod1.pin_24, Driver1.IN1
  N6: Mod1.pin_25, Driver1.IN2
  N7: Mod1.pin_26, Driver1.IN3
  N8: Mod1.pin_27, Driver1.IN4
  GND: Mod1.pin_33, Mod1.pin_38, Driver1.GND, Driver2.GND
  N9: Mod1.pin_40, Driver1.Vmotor, Driver2.Vmotor
  N10: Driver1.blue-pin, SM1.blue-pin
  N11: Driver1.pink-pin, SM1.pink-pin
  N12: Driver1.yellow-pin, SM1.yellow-pin
  N13: Driver1.orange-pin, SM1.orange-pin
  N14: Driver1.red-pin, SM1.red-pin
  N15: Driver2.blue-pin, SM2.blue-pin
  N16: Driver2.pink-pin, SM2.pink-pin
  N17: Driver2.yellow-pin, SM2.yellow-pin
  N18: Driver2.orange-pin, SM2.orange-pin
  N19: Driver2.red-pin, SM2.red-pin

custom parts:
  Raspberry Pi Pico: Raspberry Pi Pico. Based around the RP2040 microcontroller the Pico is a low cost microcontroller device bringing Raspberry Pi quality, cost, and easy of use to the microcontroller space. Jan 2021, Split part in to two versions: tht (this one) and SMD. This one will drill holes for a .1 in header in pcb to allow plugging in the module as well as providing pads to solder the module to the top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
  28BYJ-48 Driver Module: ULN2003 Driver Module for the 28BYJ-48 Unipolar Stepper Motor LED A - Blue wire - Bottom coil left LED B - Pink wire - Top coil left LED C - Yellow wire - Bottom coil right LED D - Orange wire - Top coil right Common rail - red Connector pins: blue - pink - yellow - orange - red Control pins - IN1 to IN4 Power pins - GND & Vmotor (5-12V) On/Off jumper (if removed, power to motor is cut).
  28BYJ-48 Stepper Motor: Unipolar Stepper Motor 28BYJ-48 Top coil - pink & orange Bottom coil - blue & yellow Common rail - red Connector pins: blue - pink - yellow - orange - red
  KY-040 Rotary encoder: KY-040 Rotary Encoder with switch on breakout borad from AZ Delivery
